# Fritzing sketch tessel-rgb-led-rainbow (saved by Fritzing 0.9.2b)
breadboards: 1

parts:
  Part1 = Tessel 2
  R1 = Resistor [tolerance=±5% resistance=220 package=THT]
  R2 = Resistor [tolerance=±5% resistance=220 package=THT]
  R3 = Resistor [tolerance=±5% resistance=220 package=THT]
  LED1 = RGB LED - (4 legs) [package="5 mm [THT]"]  # not connected

nets:
  N1: Part1.5#35, R1.Pin_1
  N2: Part1.5#75, R2.Pin_1
  N3: Part1.6, R3.Pin_1

custom parts:
  Tessel 2: Draft version of Tessel 2
